// Digital circuit ALU-shift-step.dig as structural Verilog
module ALU_shift_step (
  input  nCLK,
  input  nRESET,
  input  nEN,
  output SH_LOADLEN,
  output nSH_OUTPUT,
  output SH_RESET
);

  wire _74hc4017_1_p6, not_1_out;

  not not_1 (not_1_out, nRESET);
  // _74HC4017 _74hc4017_1: pin names not known; wires that end beside it: nCLK, nEN, not_1_out, SH_LOADLEN, SH_RESET, _74hc4017_1_p6
  not not_2 (nSH_OUTPUT, _74hc4017_1_p6);
endmodule

/* Test case:
CLK  ~CLK  ~EN  ~RESET    SH-LOADLEN  SH-RESET  ~{SH-OUTPUT}

#0
0    1     0    0         1           0         1
1    0     0    0         1           0         1

#1
0    1     0    1         1           0         1
1    0     0    1         1           0         1

#2
0    1     0    1         1           0         1
1    0     0    1         1           0         1

#3
0    1     0    1         1           0         1
1    0     0    1         1           0         1

#4
0    1     0    1         0           1         1
1    0     0    1         0           1         1

#5
0    1     0    1         0           0         1
1    0     0    1         0           0         1

#6
0    1     0    1         0           0         1
1    0     0    1         0           0         1

#7
0    1     0    1         0           0         1
1    0     0    1         0           0         1

#8
0    1     0    1         0           0         1
1    0     0    1         0           0         1

#9
0    1     0    1         0           0         0
1    0     0    1         0           0         0

#10
0    1     0    1         0           0         0
1    0     0    1         0           0         0

#11
0    1     0    1         0           0         0
1    0     0    1         0           0         0

#12
0    1     0    1         0           0         0
1    0     0    1         0           0         0
*/
