// Digital circuit CPU.dig as structural Verilog
module CPU (
  input  CLK_RAW,
  input  [31:0] Breakpoint,
  output [31:0] x8_s0,
  output [31:0] x9_s1,
  output [31:0] x10_a0,
  output [31:0] PC,
  output [31:0] Address,
  output [31:0] Instr,
  output [7:0] Data_Read,
  output [5:0] Step,
  output [7:0] Substep,
  output [16:0] out_10,
  output [31:0] A,
  output [31:0] B,
  output [31:0] Result,
  output [11:0] CSR_Address,
  output [31:0] x11_a1,
  output [31:0] x4_tp,
  output [31:0] x5_t0,
  output [31:0] x6_t1,
  output [31:0] x7_t2,
  output [31:0] x1_ra,
  output [31:0] x2_sp,
  output [31:0] x3_gp,
  output [31:0] x12_a2,
  output [31:0] x13_a3,
  output [31:0] x14_a4,
  output [31:0] x15_a5,
  output [31:0] mepc,
  output [31:0] mscratch,
  output [31:0] mstatus,
  output [31:0] mie,
  output [31:0] mip,
  output [31:0] mcause,
  output [10:0] out_34,
  output [31:0] mtvec,
  output [7:0] Data_Write,
  output [31:0] Instr_2,
  output [31:0] Cycles,
  output [15:0] Instr16,
  output [4:0] Val,
  output out_42,
  output Compr,
  output nOE,
  output CLK,
  output BUS_CLK,
  output nCLK
);

  wire ADDR_CLK_GATED, ADDR_IN, ADDR_LATCH, ALU_A, ALU_AUX, ALU_B, ALU_B_MUX, ALU_N, and_1_out, and_2_out,
       and_6_out, B_INSTR, B_RESET, B_RUN, B_STEP, B_STOP, B_SUBSTEP, BUS_EN, BUT_INSTR, BUT_STOP,
       button_1_out, button_2_out, CNT_2, comparator_1_eq, comparator_1_gt, comparator_1_lt, comparator_2_eq,
       CS_IO, CS_RAM, CS_ROM, CSR_ADDR_LATCH, CSR_IN, CSR_IN_LATCH, CSR_OUT, CSR_OUT_LATCH, CSR_PC_OUT,
       d_ff_1_q, d_ff_2_q, d_ff_5_q, d_ff_as_1_q, d_ff_as_4_q, d_ff_as_5_q, Imm, INT1P, INT2P, INT3P,
       LASTSTEP, LED_G, LED_R, MEM_IN, MEM_OUT, MEPC_OUT, mie_1_mei1e, mie_1_mei2e, mie_1_mei3e, MIE_t,
       mip_1_mei1p, mip_1_mei2p, mip_1_mei3p, MRET, MTVEC_OUT, multiplexer_4_out, multiplexer_7_out,
       nALU_RESET, nand_1_out, nILL_OP, nIRQ, nKB_INT, nLEN8, nMEM_OE, nMEM_OE_OUT, nMEM_WE, nMEM_WE_OUT,
       not_2_out, not_3_out, not_4_out, nREG_IN_EN, nRESET, nS_EXT, nSLEEP, nWAIT, OP_FETCH, OP_IMM_LATCH,
       OP_IN, OP_IN_MUX, OP_LATCH, OP_LATCH_LSB, OPDONE, or_2_out, PC_IN, PC_IN_LATCH, PC_IN_MUX, PC_OUT,
       PC_OUT_LATCH, REG_IN, RESET, reset_2_out, RS1, STEPDONE, switch_1_a, switchdt_1_p3, TRAP_OP, WAKEUP;
  wire [0:0] LEN;
  wire [1:0] ALU_A_MUX, REG_IN_MUX, TRAP2;
  wire [2:0] ALU_OP, IMM_MUX;
  wire [3:0] RSA, RSB, RSD;
  wire [7:0] DATA, Mem_Dval;
  wire [20:8] MicroCode_d;
  wire [31:0] DATA_ADDR;

  // RGBLED rgbled_1: pin names not known; wires that end beside it: LED_R, LED_G, 1'b0
  Comparator #(.Bits(32)) comparator_1 (
    .a(x3_gp), .b(32'h1), .gt(comparator_1_gt), .eq(comparator_1_eq), .lt(comparator_1_lt));
  and and_1 (and_1_out, nIRQ, nILL_OP);
  // RGBLED rgbled_2: pin names not known; wires that end beside it: comparator_1_gt, comparator_1_eq, comparator_1_lt
  Comparator #(.Bits(32)) comparator_2 (.a(Breakpoint), .b(PC), .eq(comparator_2_eq));  // open: gt, lt
  Button #(.activeLow("true")) Stop (.out(BUT_STOP));
  Button #(.activeLow("true")) Run (.out(B_RUN));
  Button #(.activeLow("true")) u_Reset (.out(B_RESET));
  Switch switch_1 (.A(switch_1_a), .B(comparator_1_lt));
  D_FF d_ff_1 (.D(comparator_2_eq), .C(~OPDONE), .Q(d_ff_1_q));  // open: nQ
  Interrupt_Controller interrupt_controller_1 (
    .BUS_CLK(BUS_CLK), .OP_FETCH(OP_LATCH), .nTRAP(and_1_out), .nRESET(nRESET), .TRAP_OP(TRAP_OP),
    .TRAP_OP_FETCH(OP_IN_MUX));
  PullUp pullup_1 (.out(switch_1_a));
  D_FF_AS #(.Default(1)) d_ff_as_1 (.Set(nCLK), .D(1'b0), .C(d_ff_1_q), .Clr(1'b0), .Q(d_ff_as_1_q));  // open: nQ
  Button #(.activeLow("true")) One_Instruction (.out(BUT_INSTR));
  Button #(.activeLow("true")) One_Step (.out(B_STEP));
  Button #(.activeLow("true")) One_Substep (.out(B_SUBSTEP));
  D_FF #(.Default(1)) d_ff_2 (.D(switch_1_a), .C(OPDONE), .Q(d_ff_2_q));  // open: nQ
  DiodeBackward diodebackward_1 (.in(d_ff_2_q), .out(B_STOP));
  DiodeBackward diodebackward_2 (.in(BUT_STOP), .out(B_STOP));
  DiodeBackward diodebackward_3 (.in(d_ff_as_1_q), .out(B_INSTR));
  DiodeBackward diodebackward_4 (.in(BUT_INSTR), .out(B_INSTR));
  PullUp pullup_2 (.out(B_STOP));
  PullUp pullup_3 (.out(B_INSTR));
  ALU alu_1 (
    .BUS_CLK(BUS_CLK), .A(ALU_A), .B(ALU_B), .N(ALU_N), .ALU_nRESET(nALU_RESET), .ALU_AUX(ALU_AUX),
    .S(ALU_OP), .FLAG(out_10[16]), .OUT(ADDR_IN));  // open: DLEN, DSUM, C
  and and_2 (and_2_out, CNT_2, OP_LATCH_LSB);
  nand nand_1 (nand_1_out, nOE, nMEM_WE);
  nand nand_2 (nLEN8, LEN[0], BUS_EN);
  Mem mem_1 (
    .CLK(CLK), .BUS_CLK(BUS_CLK), .IN(MEM_IN), .ADDR_IN(ADDR_IN), .ADDR_LATCH(ADDR_LATCH),
    .ADDR_CLK(ADDR_CLK_GATED), .nOE(nOE), .nWE(nMEM_WE), .nS_EXT(nS_EXT), .nRESET(nRESET), .OUT(MEM_OUT),
    .DATA(DATA), .DATA_ADDR(DATA_ADDR), .DAddr(Address), .DVal(Mem_Dval), .nMEM_OE_OUT(nMEM_OE_OUT),
    .nMEM_WE_OUT(nMEM_WE_OUT));  // open: DIn
  D_FF #(.Bits(8)) d_ff_3 (.D(DATA), .C(nMEM_OE_OUT), .Q(Data_Read));  // open: nQ
  D_FF #(.Bits(8)) d_ff_4 (.D(DATA), .C(nMEM_WE_OUT), .Q(Data_Write));  // open: nQ
  Clock_driver clock_driver_1 (
    .CLK_RAW(CLK_RAW), .Stop(B_STOP), .Run(B_RUN), .One_Instruction(B_INSTR), .One_Step(B_STEP),
    .One_Substep(B_SUBSTEP), .nSTEPDONE(STEPDONE), .nOPDONE(OPDONE), .nRESET(RESET), .nWAKEUP(WAKEUP),
    .SLEEP(nSLEEP), .nWAIT(nWAIT), .CLK(CLK), .nCLK(nCLK), .LED_R(LED_R), .LED_G(LED_G));
  Reset reset_2 (.out(reset_2_out));
  and and_3 (nRESET, reset_2_out, B_RESET);
  or or_1 (nOE, nMEM_OE, and_2_out);
  D_FF d_ff_5 (.D(nand_1_out), .C(nCLK), .Q(d_ff_5_q));  // open: nQ
  not not_1 (RESET, nRESET);
  or or_2 (or_2_out, d_ff_5_q, ADDR_LATCH);
  nor nor_1 (LASTSTEP, LEN[0], BUS_EN);
  DebugShift32 debugshift32_1 (.CLK(BUS_CLK), .D(ALU_A), .nEN(1'b0), .Val(A));
  DebugShift32 debugshift32_2 (.CLK(BUS_CLK), .D(ALU_B), .nEN(1'b0), .Val(B));
  DebugShift32 debugshift32_3 (.CLK(BUS_CLK), .D(ADDR_IN), .nEN(1'b0), .Val(Result));
  PullUp pullup_4 (.out(nWAIT));
  D_FF d_ff_6 (.D(or_2_out), .C(nCLK), .Q(ADDR_CLK_GATED));  // open: nQ
  Clock clock_1 (
    .CLK(CLK), .nCLK(nCLK), .nLEN4(nLEN8), .LASTSTEP(LASTSTEP), .nRESET(nRESET), .STEP(out_10[5:0]),
    .STEPDONE(STEPDONE), .SUBSTEP(Substep), .OPDONE(OPDONE));
  // SwitchDT switchdt_1: pin names not known; wires that end beside it: nMEM_WE_OUT, 1'b1, switchdt_1_p3
  Terminal terminal_1 (
    .A(DATA_ADDR[15:0]), .nCS(CS_IO), .nWE(nMEM_WE_OUT), .nOE(nMEM_OE_OUT), .D(DATA), .nINT(nKB_INT));
  and and_4 (BUS_CLK, CLK, BUS_EN);
  EEPROM #(.AddrBits(16), .Bits(8)) Firmware (
    .A(DATA_ADDR[15:0]), .CS(~CS_ROM), .WE(~switchdt_1_p3), .OE(~nMEM_OE_OUT), .D(DATA));
  RAMSinglePortSel #(.AddrBits(16), .Bits(8)) RAM (
    .A(DATA_ADDR[15:0]), .CS(~CS_RAM), .WE(~nMEM_WE_OUT), .OE(~nMEM_OE_OUT), .D(DATA));
  Demultiplexer #(.Selector_Bits(2), .Default(1)) demultiplexer_1 (
    .sel(DATA_ADDR[31:30]), .in(1'b0), .out_0(CS_ROM), .out_2(CS_RAM), .out_3(CS_IO));  // open: out_1
  OpCode opcode_1 (
    .BUS_CLK(BUS_CLK), .IN(OP_IN), .OP_LATCH(OP_LATCH), .OP_LATCH_LSB(OP_LATCH_LSB),
    .IMM_LATCH(OP_IMM_LATCH), .IMM_SnP(out_42), .IMM_MUX(IMM_MUX), .nRESET(nRESET), .OP_FETCH(OP_FETCH),
    .IMM(Imm), .RSA(RSA), .RSB(RSB), .RD(RSD), .OPCODE(out_10[10:6]), .FUNC3(out_10[13:11]),
    .ALU_SA(out_10[15]), .nS_EXT(nS_EXT), .SYS(out_10[14]), .TRAP2(TRAP2), .CNT_2(CNT_2), .Instr(Instr),
    .Instr16(Instr16), .Compr(Compr));
  D_FF_AS d_ff_as_2 (.Set(~1'b1), .D(LASTSTEP), .C(nCLK), .Clr(~nRESET), .Q(OP_LATCH));  // open: nQ
  ROM #(.AddrBits(17), .isProgramMemory("true"), .Bits(32)) MicroCode (
    .A(out_10), .sel(1'b1),
    .D({REG_IN_MUX, IMM_MUX, ALU_A_MUX, PC_IN_MUX, CSR_IN_LATCH, CSR_OUT_LATCH, CSR_ADDR_LATCH, MicroCode_d[20:18], nALU_RESET, ALU_AUX, ALU_OP, ALU_N, nREG_IN_EN, nMEM_WE, nMEM_OE, MicroCode_d[8], ADDR_LATCH, nILL_OP, PC_OUT_LATCH, PC_IN_LATCH, OP_FETCH, nSLEEP, BUS_EN, LEN[0]}));
  D_FF_AS d_ff_as_3 (.Set(~1'b1), .D(OP_LATCH), .C(CLK), .Clr(~nRESET), .Q(OP_IMM_LATCH));  // open: nQ
  Multiplexer multiplexer_1 (.sel(OP_IN_MUX), .in_0(MEM_OUT), .in_1(TRAP_OP), .out(OP_IN));
  Multiplexer multiplexer_2 (.sel(PC_IN_MUX), .in_0(ADDR_IN), .in_1(CSR_PC_OUT), .out(PC_IN));
  Multiplexer #(.Selector_Bits(2)) multiplexer_3 (
    .sel(REG_IN_MUX), .in_0(ADDR_IN), .in_1(MEM_OUT), .in_2(CSR_IN), .in_3(PC_OUT), .out(REG_IN));
  not not_2 (not_2_out, BUS_CLK);
  _74HC4024 _74hc4024_1 (
    .CP(not_2_out), .MR(RESET), .Q0(Val[0]), .Q1(Val[1]), .Q2(Val[2]), .Q3(Val[3]), .Q4(Val[4]));  // open: Q5, Q6
  or or_3 (out_42, BUS_EN, Val[3], Val[4]);
  Multiplexer multiplexer_4 (.sel(ALU_A_MUX[0]), .in_0(RS1), .in_1(PC_OUT), .out(multiplexer_4_out));
  Multiplexer multiplexer_5 (.sel(ALU_B_MUX), .in_0(MEM_IN), .in_1(Imm), .out(ALU_B));
  and and_5 (OP_LATCH_LSB, Val[4], OP_FETCH);
  Multiplexer multiplexer_6 (.sel(ALU_A_MUX[1]), .in_0(multiplexer_4_out), .in_1(ALU_A_MUX[0]), .out(ALU_A));
  or or_4 (ALU_B_MUX, IMM_MUX[0], IMM_MUX[1], IMM_MUX[2]);
  PC pc_1 (
    .CLK(CLK), .BUS_CLK(BUS_CLK), .IN(PC_IN), .IN_LATCH(PC_IN_LATCH), .OUT_LATCH(PC_OUT_LATCH),
    .OUT_SnP(out_42), .CNT_EN(OP_LATCH), .CNT_2(CNT_2), .nRESET(nRESET), .OUT(PC_OUT), .PC(PC));
  Register_bank register_bank_1 (
    .CLK(BUS_CLK), .IN(REG_IN), .nEN_IN(nREG_IN_EN), .SA(RSA), .SB(RSB), .SD(RSD), .RESET(RESET), .A(RS1),
    .B(MEM_IN));
  Register_view register_view_1 (
    .BUS_CLK(BUS_CLK), .nREG_IN_EN(nREG_IN_EN), .REG_IN(REG_IN), .RSD(RSD), .x1_ra(x1_ra), .x2_sp(x2_sp),
    .x3_gp(x3_gp), .x4_tp(x4_tp), .x5_t0(x5_t0), .x6_t1(x6_t1), .x7_t2(x7_t2), .x8_s0_fp(x8_s0),
    .x9_s1(x9_s1), .x10_a0(x10_a0), .x11_a1(x11_a1), .x12_a2(x12_a2), .x13_a3(x13_a3), .x14_a4(x14_a4),
    .x15_a5(x15_a5));
  Button #(.activeLow("true")) button_1 (.out(button_1_out));
  Button #(.activeLow("true")) button_2 (.out(button_2_out));
  not not_3 (not_3_out, MRET);
  Multiplexer multiplexer_7 (.sel(out_10[13]), .in_0(RS1), .in_1(Imm), .out(multiplexer_7_out));
  PullDown pulldown_1 (.out(CSR_IN));
  and and_6 (and_6_out, not_3_out, PC_IN_MUX);
  D_FF_AS #(.Default(1)) d_ff_as_4 (.Set(CLK), .D(1'b0), .C(PC_IN_MUX), .Clr(1'b0), .Q(d_ff_as_4_q));  // open: nQ
  Counter #(.Bits(32)) counter_1 (.en(1'b1), .C(CLK), .clr(1'b0), .out(Cycles));  // open: ovf
  MIE mie_1 (
    .CLK(CLK), .BUS_CLK(BUS_CLK), .CSR_IN(CSR_OUT), .CSR_IN_LATCH(CSR_IN_LATCH),
    .CSR_OUT_LATCH(CSR_OUT_LATCH), .CSR_ADDR(CSR_Address), .nRESET(nRESET), .CSR_OUT(CSR_IN), .mie(mie),
    .MEI1E(mie_1_mei1e), .MEI2E(mie_1_mei2e), .MEI3E(mie_1_mei3e));
  MIP mip_1 (
    .CLK(CLK), .BUS_CLK(BUS_CLK), .CSR_IN(CSR_OUT), .CSR_IN_LATCH(CSR_IN_LATCH),
    .CSR_OUT_LATCH(CSR_OUT_LATCH), .CSR_ADDR(CSR_Address), .nINT1(nKB_INT), .nINT2(button_1_out),
    .nINT3(button_2_out), .nRESET(nRESET), .CSR_OUT(CSR_IN), .mip(mip), .MEI1P(mip_1_mei1p),
    .MEI2P(mip_1_mei2p), .MEI3P(mip_1_mei3p));
  CSR csr_1 (
    .CLK(BUS_CLK), .INA(multiplexer_7_out), .INB(CSR_IN), .CSR_FUNC(out_10[12:11]), .ADDR_IN(Imm),
    .ADDR_LATCH(CSR_ADDR_LATCH), .nRESET(nRESET), .NEW_VAL(CSR_OUT), .ADDR(CSR_Address));
  MEPC mepc_1 (
    .BUS_CLK(BUS_CLK), .PC_IN(PC_OUT), .IN_EN(and_6_out), .CSR_IN(CSR_OUT), .CSR_IN_LATCH(CSR_IN_LATCH),
    .CSR_ADDR(CSR_Address), .RESET(RESET), .OUT(MEPC_OUT), .CSR_OUT(CSR_IN), .mepc(mepc));
  MSTATUS mstatus_1 (
    .CLK(CLK), .BUS_CLK(BUS_CLK), .CSR_IN(CSR_OUT), .CSR_IN_LATCH(CSR_IN_LATCH),
    .CSR_OUT_LATCH(CSR_OUT_LATCH), .CSR_ADDR(CSR_Address), .IRQ(PC_IN_MUX), .MRET(MRET),
    .IRQ_LATCH(d_ff_as_4_q), .RESET(RESET), .nRESET(nRESET), .CSR_OUT(CSR_IN), .mstatus(mstatus), .MIE(MIE_t));  // open: MPIE
  Counter #(.Bits(32)) counter_2 (.en(1'b1), .C(OPDONE), .clr(1'b0), .out(Instr_2));  // open: ovf
  D_FF_AS #(.Default(1)) d_ff_as_5 (.Set(CLK), .D(MRET), .C(PC_IN_MUX), .Clr(1'b0), .Q(d_ff_as_5_q));  // open: nQ
  and and_7 (INT1P, mie_1_mei1e, mip_1_mei1p);
  and and_8 (INT2P, mie_1_mei2e, mip_1_mei2p);
  and and_9 (INT3P, mie_1_mei3e, mip_1_mei3p);
  not not_4 (not_4_out, TRAP2[0]);
  MTVEC mtvec_1 (
    .BUS_CLK(BUS_CLK), .MTVEC_SnP(PC_IN_MUX), .CSR_IN(CSR_OUT), .CSR_IN_LATCH(CSR_IN_LATCH),
    .CSR_ADDR(CSR_Address), .RESET(RESET), .MTVEC_OUT(MTVEC_OUT), .CSR_OUT(CSR_IN), .mtvec(mtvec));
  MSCRATCH mscratch_1 (
    .BUS_CLK(BUS_CLK), .CSR_IN(CSR_OUT), .CSR_IN_LATCH(CSR_IN_LATCH), .CSR_ADDR(CSR_Address), .RESET(RESET),
    .CSR_OUT(CSR_IN), .mscratch(mscratch));
  and and_10 (MRET, not_4_out, TRAP2[1]);
  MCAUSE mcause_1 (
    .BUS_CLK(BUS_CLK), .CSR_IN_LATCH(CSR_IN_LATCH), .CSR_OUT_LATCH(CSR_OUT_LATCH), .CSR_ADDR(CSR_Address),
    .TRAP2(TRAP2), .nIRQ(nIRQ), .INT1P(INT1P), .INT2P(INT2P), .INT3P(INT3P), .IRQ_LATCH(d_ff_as_5_q),
    .nRESET(nRESET), .CSR_OUT(CSR_IN), .mcause(mcause));
  DiodeForward diodeforward_1 (.in(INT1P), .out(WAKEUP));
  DiodeForward diodeforward_2 (.in(INT2P), .out(WAKEUP));
  DiodeForward diodeforward_3 (.in(INT3P), .out(WAKEUP));
  Multiplexer multiplexer_8 (.sel(MRET), .in_0(MTVEC_OUT), .in_1(MEPC_OUT), .out(CSR_PC_OUT));
  PullDown pulldown_2 (.out(WAKEUP));
  nand nand_3 (nIRQ, MIE_t, WAKEUP);

  assign out_34 = out_10[16:6];
  assign Step = out_10[5:0];

  // Other names for the same wires on the sheet: LEN[1] = BUS_EN; ALU_OUT = ADDR_IN; CntCycles[31:0] = Cycles;
  //   CntInstr[31:0] = Instr_2; CSR_ADDR[11:0] = CSR_Address; Da[31:0] = A; DATA_ADDR_16[15:0] = DATA_ADDR[15:0];
  //   Db[31:0] = B; Dres[31:0] = Result; FLAG = out_10[16]; FUNC3[2:0] = out_10[13:11]; Mem_Addr[31:0] = Address;
  //   Mem_Data_R[7:0] = Data_Read; Mem_Data_W[7:0] = Data_Write; nMEM_OE_GATED = nOE; OPCODE[4:0] = out_10[10:6];
  //   PC_CNT_EN = OP_LATCH; IMM_PC_OUT_SnP = out_42; IMM_SnP = out_42; PC_OUT_SnP = out_42; RS2 = MEM_IN;
  //   SA = out_10[15]; SYS = out_10[14]; x1[31:0] = x1_ra; x2[31:0] = x2_sp; x3[31:0] = x3_gp; x4[31:0] = x4_tp;
  //   x5[31:0] = x5_t0; x6[31:0] = x6_t1; x7[31:0] = x7_t2; x8[31:0] = x8_s0; x9[31:0] = x9_s1; x10[31:0] = x10_a0;
  //   x11[31:0] = x11_a1; x12[31:0] = x12_a2; x13[31:0] = x13_a3; x14[31:0] = x14_a4; x15[31:0] = x15_a5

  // Notes on the sheet:
  //   CLK_RAW: Hz: 50000
  //   Breakpoint: default 4294967295
  //   Debug
  //   Interrupts
  //   Clock
  //   ALU
  //   Memory
  //   contents of Firmware (hex, n*v repeats v):
  //   81,40,1,41,33,87,20,0,81,43,b7,4,2,0,89,4,5,4,63,4,77,0,6f,70
  //   ,80,78,85,40,5,41,33,87,20,0,89,43,b7,4,2,0,8d,4,5,4,63,4,77,0
  //   ,6f,70,e0,76,8d,40,1d,41,33,87,20,0,a9,43,b7,4,2,0,91,4,5,4,63
  //   ,4,77,0,6f,70,40,75,81,40,37,81,ff,ff,33,87,20,0,e1,73,b7,4,2
  //   ,0,95,4,5,4,63,4,77,0,6f,70,80,73,b7,0,0,80,1,41,33,87,20,0,b7
  //   ,3,0,80,b7,4,2,0,99,4,5,4,63,4,77,0,6f,70,a0,71,b7,0,0,80,37,81
  //   ,ff,ff,33,87,20,0,b7,83,ff,7f,b7,4,2,0,9d,4,5,4,63,4,77,0,6f,70
  //   ,a0,6f,81,40,37,81,0,0,7d,11,33,87,20,0,a1,63,fd,13,b7,4,2,0,a1
  //   ,4,5,4,63,4,77,0,6f,70,a0,6d,b7,0,0,80,fd,10,1,41,33,87,20,0,b7
  //   ,3,0,80,fd,13,b7,4,2,0,a5,4,5,4,63,4,77,0,6f,70,80,6b,b7,0,0,80
  //   ,fd,10,37,81,0,0,7d,11,33,87,20,0,b7,83,0,80,f9,13,b7,4,2,0,a9
  //   ,4,5,4,63,4,77,0,6f,70,20,69,b7,0,0,80,37,81,0,0,7d,11,33,87,20
  //   ,0,b7,83,0,80,fd,13,b7,4,2,0,ad,4,5,4,63,4,77,0,6f,70,e0,66,b7
  //   ,0,0,80,fd,10,37,81,ff,ff,33,87,20,0,b7,83,ff,7f,fd,13,b7,4,2
  //   ,0,b1,4,5,4,63,4,77,0,6f,70,a0,64,81,40,13,1,f0,ff,33,87,20,0
  //   ,93,3,f0,ff,b7,4,2,0,b5,4,5,4,63,4,77,0,6f,70,c0,62,93,0,f0,ff
  //   ,5,41,33,87,20,0,81,43,b7,4,2,0,b9,4,5,4,63,4,77,0,6f,70,0,61
  //   ,93,0,f0,ff,13,1,f0,ff,33,87,20,0,93,3,e0,ff,b7,4,2,0,bd,4,5,4
  //   ,63,4,77,0,6f,70,0,5f,85,40,37,1,0,80,7d,11,33,87,20,0,b7,3,0
  //   ,80,b7,4,2,0,c1,4,5,4,63,4,77,0,6f,70,0,5d,b5,40,2d,41,8a,90,e1
  //   ,43,b7,4,2,0,c5,4,5,4,63,84,70,0,6f,70,80,5b,b9,40,2d,41,6,91
  //   ,e5,43,b7,4,2,0,c9,4,5,4,63,4,71,0,6f,70,0,5a,b5,40,86,90,e9,43
  //   ,b7,4,2,0,cd,4,5,4,63,84,70,0,6f,70,a0,58,1,42,b5,40,2d,41,33
  //   ,87,20,0,13,3,7,0,5,2,89,42,e3,18,52,fe,e1,43,b7,4,2,0,d1,4,5
  //   ,4,63,4,73,0,6f,70,20,56,1,42,b9,40,2d,41,33,87,20,0,1,0,13,3
  //   ,7,0,5,2,89,42,e3,17,52,fe,e5,43,b7,4,2,0,d5,4,5,4,63,4,73,0,6f
  //   ,70,80,53,1,42,bd,40,2d,41,33,87,20,0,1,0,1,0,13,3,7,0,5,2,89
  //   ,42,e3,16,52,fe,e9,43,b7,4,2,0,d9,4,5,4,63,4,73,0,6f,70,c0,50
  //   ,1,42,b5,40,2d,41,33,87,20,0,5,2,89,42,e3,1a,52,fe,e1,43,b7,4
  //   ,2,0,dd,4,5,4,63,4,77,0,6f,70,80,4e,1,42,b9,40,2d,41,1,0,33,87
  //   ,20,0,5,2,89,42,e3,19,52,fe,e5,43,b7,4,2,0,e1,4,5,4,63,4,77,0
  //   ,6f,70,20,4c,1,42,bd,40,2d,41,1,0,1,0,33,87,20,0,5,2,89,42,e3
  //   ,18,52,fe,e9,43,b7,4,2,0,e5,4,5,4,63,4,77,0,6f,70,a0,49,1,42,b5
  //   ,40,1,0,2d,41,33,87,20,0,5,2,89,42,e3,19,52,fe,e1,43,b7,4,2,0
  //   ,e9,4,5,4,63,4,77,0,6f,70,40,47,1,42,b9,40,1,0,2d,41,1,0,33,87
  //   ,20,0,5,2,89,42,e3,18,52,fe,e5,43,b7,4,2,0,ed,4,5,4,63,4,77,0
  //   ,6f,70,c0,44,1,42,bd,40,1,0,1,0,2d,41,33,87,20,0,5,2,89,42,e3
  //   ,18,52,fe,e9,43,b7,4,2,0,f1,4,5,4,63,4,77,0,6f,70,40,42,1,42,2d
  //   ,41,b5,40,33,87,20,0,5,2,89,42,e3,1a,52,fe,e1,43,b7,4,2,0,f5,4
  //   ,5,4,63,4,77,0,6f,70,0,40,1,42,2d,41,b9,40,1,0,33,87,20,0,5,2
  //   ,89,42,e3,19,52,fe,e5,43,b7,4,2,0,f9,4,5,4,63,4,77,0,6f,70,a0
  //   ,3d,1,42,2d,41,bd,40,1,0,1,0,33,87,20,0,5,2,89,42,e3,18,52,fe
  //   ,e9,43,b7,4,2,0,fd,4,5,4,63,4,77,0,6f,70,20,3b,1,42,2d,41,1,0
  //   ,b5,40,33,87,20,0,5,2,89,42,e3,19,52,fe,e1,43,b7,4,2,0,93,84,4
  //   ,2,5,4,63,4,77,0,6f,70,a0,38,1,42,2d,41,1,0,b9,40,1,0,33,87,20
  //   ,0,5,2,89,42,e3,18,52,fe,e5,43,b7,4,2,0,93,84,14,2,5,4,63,4,77
  //   ,0,6f,70,0,36,1,42,2d,41,1,0,1,0,bd,40,33,87,20,0,5,2,89,42,e3
  //   ,18,52,fe,e9,43,b7,4,2,0,93,84,24,2,5,4,63,4,77,0,6f,70,60,33
  //   ,bd,40,33,1,10,0,bd,43,b7,4,2,0,93,84,34,2,5,4,63,4,71,0,6f,70
  //   ,c0,31,93,0,0,2,33,81,0,0,93,3,0,2,b7,4,2,0,93,84,44,2,5,4,63
  //   ,4,71,0,6f,70,e0,2f,b3,0,0,0,81,43,b7,4,2,0,93,84,54,2,5,4,63
  //   ,84,70,0,6f,70,60,2e,c1,40,79,41,33,80,20,0,81,43,b7,4,2,0,93
  //   ,84,64,2,5,4,63,4,70,0,6f,70,a0,2c,81,40,1,41,33,87,20,40,81,43
  //   ,b7,4,3,0,89,4,5,4,63,4,77,0,6f,70,0,2b,85,40,5,41,33,87,20,40
  //   ,81,43,b7,4,3,0,8d,4,5,4,63,4,77,0,6f,70,60,29,8d,40,1d,41,33
  //   ,87,20,40,93,3,c0,ff,b7,4,3,0,91,4,5,4,63,4,77,0,6f,70,a0,27,81
  //   ,40,37,81,ff,ff,33,87,20,40,a1,63,b7,4,3,0,95,4,5,4,63,4,77,0
  //   ,6f,70,e0,25,b7,0,0,80,1,41,33,87,20,40,b7,3,0,80,b7,4,3,0,99
  //   ,4,5,4,63,4,77,0,6f,70,0,24,b7,0,0,80,37,81,ff,ff,33,87,20,40
  //   ,b7,83,0,80,b7,4,3,0,9d,4,5,4,63,4,77,0,6f,70,0,22,81,40,37,81
  //   ,0,0,7d,11,33,87,20,40,e1,73,85,3,b7,4,3,0,a1,4,5,4,63,4,77,0
  //   ,6f,70,0,20,b7,0,0,80,fd,10,1,41,33,87,20,40,b7,3,0,80,fd,13,b7
  //   ,4,3,0,a5,4,5,4,63,4,77,0,6f,70,e0,1d,b7,0,0,80,fd,10,37,81,0,0
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  //   Microcode
  //   Opcode
  //   Muxes
  //   contents of MicroCode (hex, n*v repeats v):
  //   a10e45,4*8a30e47,a30ee5,a30e45,a30c45,4*72a32647,a306c5,a30645
  //   ,a30c6d,a30e4f,a30c4d,a30e4f,a30c4d,a30e4f,a30c4d,a30e4f,a30e44,a30e44
  //   ,40*0,a30e45,a30e05,4*32a32e07,a30e85,a30e05,a30c0d,a30e0f,a30c0d
  //   ,a30e0f,a30c0d,a30e0f,a30c0d,a30e0f,a30e04,a30e04,46*0,a30e45
  //   ,a30e05,4*32a32e07,a30e85,a30e05,a30c0d,a30e0f,a30c0d,a30e0f,a30c0d
  //   ,a30e0f,a30c0d,a30e0f,a30e04,a30e04,46*0,a30e4d,a30c6d,a30e4f
  //   ,a30c4d,a30e4f,a30c4d,a30e4f,a30c4d,a30e4f,a30e44,a30e44,53*0
  //   ,a10c4d,8a3064f,8a3046d,8a3064f,8a3044d,8a3064f,8a3044d,8a3064f
  //   ,a30e44,a30e44,54*0,a10c4d,22a3064f,22a3046d,22a3064f,22a3044d
  //   ,22a3064f,22a3044d,22a3064f,a30e44,a30e44,54*0,a30e45,a30e05,4*32a32e07
  //   ,a30e85,a30e05,a30c0d,a30e0f,a30c0d,a30e0f,a30c0d,a30e0f,a30c0d
  //   ,a30e0f,a30e04,a30e04,46*0,a30e45,a30e05,4*32a32e07,a30e85,a30e05
  //   ,a30c0d,a30e0f,a30c0d,a30e0f,a30c0d,a30e0f,a30c0d,a30e0f,a30e04,a30e04
  //   ,46*0,a10e45,4*10a30e47,a30ee5,32a32e47,32a32a45,32a32e47,32a32e47,32a32e47
  //   ,a30ec5,a30e45,a30c6d,a30e4f,a30c4d,a30e4f,a30c4d,a30e4f,a30c4d
  //   ,a30e4f,a30e44,a30e44,41*0,a30e45,a30e05,4*32a32e07,a30e85,a30e05
  //   ,a30c0d,a30e0f,a30c0d,a30e0f,a30c0d,a30e0f,a30c0d,a30e0f,a30e04,a30e04
  //   ,46*0,a30e45,a30e05,4*32a32e07,a30e85,a30e05,a30c0d,a30e0f,a30c0d
  //   ,a30e0f,a30c0d,a30e0f,a30c0d,a30e0f,a30e04,a30e04,46*0,a30e45
  //   ,a30e05,4*32a32e07,a30e85,a30e05,a30c0d,a30e0f,a30c0d,a30e0f,a30c0d
  //   ,a30e0f,a30c0d,a30e0f,a30e04,a30e04,46*0,a10c4d,a3064f,a3046d
  //   ,a3064f,a3044d,a3064f,a3044d,a3064f,a30e44,a30e44,54*0,a10c4d
  //   ,24a3064f,24a3046d,24a3064f,24a3044d,24a3064f,24a3044d,24a3064f
  //   ,a30e44,a30e44,54*0,a30e45,a30e05,4*32a32e07,a30e85,a30e05,a30c0d
  //   ,a30e0f,a30c0d,a30e0f,a30c0d,a30e0f,a30c0d,a30e0f,a30e04,a30e04
  //   ,46*0,a30e45,a30e05,4*32a32e07,a30e85,a30e05,a30c0d,a30e0f,a30c0d
  //   ,a30e0f,a30c0d,a30e0f,a30c0d,a30e0f,a30e04,a30e04,46*0,a30e45
  //   ,a30e05,4*32a32e07,a30e85,a30e05,a30c0d,a30e0f,a30c0d,a30e0f,a30c0d
  //   ,a30e0f,a30c0d,a30e0f,a30e04,a30e04,46*0,a30e45,a30e05,4*32a32e07
  //   ,a30e85,a30e05,a30c0d,a30e0f,a30c0d,a30e0f,a30c0d,a30e0f,a30c0d
  //   ,a30e0f,a30e04,a30e04,46*0,a30e45,a30e05,4*32a32e07,a30e85,a30e05
  //   ,a30c0d,a30e0f,a30c0d,a30e0f,a30c0d,a30e0f,a30c0d,a30e0f,a30e04,a30e04
  //   ,46*0,a30e45,a30e05,4*32a32e07,a30e85,a30e05,a30c0d,a30e0f,a30c0d
  //   ,a30e0f,a30c0d,a30e0f,a30c0d,a30e0f,a30e04,a30e04,46*0,a30e45
  //   ,a30e05,4*32a32e07,a30e85,a30e05,a30c0d,a30e0f,a30c0d,a30e0f,a30c0d
  //   ,a30e0f,a30c0d,a30e0f,a30e04,a30e04,46*0,a30e45,a30e05,4*32a32e07
  //   ,a30e85,a30e05,a30c0d,a30e0f,a30c0d,a30e0f,a30c0d,a30e0f,a30c0d
  //   ,a30e0f,a30e04,a30e04,46*0,a30e45,a30e05,4*32a32e07,a30e85,a30e05
  //   ,a30c0d,a30e0f,a30c0d,a30e0f,a30c0d,a30e0f,a30c0d,a30e0f,a30e04,a30e04
  //   ,46*0,a30e45,a30e05,4*32a32e07,a30e85,a30e05,a30c0d,a30e0f,a30c0d
  //   ,a30e0f,a30c0d,a30e0f,a30c0d,a30e0f,a30e04,a30e04,46*0,a11e45
  //   ,4*a25e47,a30e45,a30c6d,a30e4f,a30c4d,a30e4f,a30c4d,a30e4f,a30c4d
  //   ,a30e4f,a30e44,a30e44,48*0,a10e45,4*8a30e47,a10ee5,a10e55,a10c4d
  //   ,32a3264f,32a3244d,32a3264f,32a3244d,32a3264f,32a3244d,32a3264f
  //   ,a30e64,a30e64,47*0,a30e45,a30e05,4*32a32e07,a30e85,a30e05,a30c0d
  //   ,a30e0f,a30c0d,a30e0f,a30c0d,a30e0f,a30c0d,a30e0f,a30e04,a30e04
  //   ,46*0,a10e45,4*2aa30e47,a10ee5,a10e55,a10c4d,32a3264f,32a3244d
  //   ,32a3264f,32a3244d,32a3264f,32a3244d,32a3264f,a30e64,a30e64,47*0
  //   ,a30e45,4*1a30e47,a30e55,a30e65,4*32a32e47,a30ec5,a30e45,a30c4d
  //   ,a30e4f,a30c4d,a30e4f,a30c4d,a30e4f,a30c4d,a30e4f,a30e44,a30e44
  //   ,41*0,a30e45,a30e05,4*32a32e07,a30e85,a30e05,a30c0d,a30e0f,a30c0d
  //   ,a30e0f,a30c0d,a30e0f,a30c0d,a30e0f,a30e04,a30e04,46*0,a30e45
  //   ,a30e05,4*32a32e07,a30e85,a30e05,a30c0d,a30e0f,a30c0d,a30e0f,a30c0d
  //   ,a30e0f,a30c0d,a30e0f,a30e04,a30e04,46*0,a30e45,a30e05,4*32a32e07
  //   ,a30e85,a30e05,a30c0d,a30e0f,a30c0d,a30e0f,a30c0d,a30e0f,a30c0d
  //   ,a30e0f,a30e04,a30e04,46*0,a10e45,4*8a30e47,a30ee5,a30e45,a30c45
  //   ,72a32647,72a32445,72a32647,72a32647,72a32647,a306c5,a30645,a30c6d
  //   ,a30e4f,a30c4d,a30e4f,a30c4d,a30e4f,a30c4d,a30e4f,a30e44,a30e44
  //   ,39*0,a30e45,a30e05,4*32a32e07,a30e85,a30e05,a30c0d,a30e0f,a30c0d
  //   ,a30e0f,a30c0d,a30e0f,a30c0d,a30e0f,a30e04,a30e04,46*0,a30e45
  //   ,a30e05,4*32a32e07,a30e85,a30e05,a30c0d,a30e0f,a30c0d,a30e0f,a30c0d
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  //   Note: we assume that bus cycles 
  //   always come in groups of at least 8.
  //   Hence we only need to check the
  //   upper two bits of the counter.
  //   PC
  //   Registers
  //   CSR
endmodule
