// Digital circuit Clock.dig as structural Verilog
module Clock (
  input  CLK,
  input  nCLK,
  input  [1:0] LEN,
  input  LASTSTEP,
  input  nRESET,
  output [4:0] STEP,
  output LASTSUBSTEP,
  output nSTEPDONE,
  output [7:0] SUBSTEP,
  output nOPDONE
);

  wire and_1_out, not_1_out, substep_counter_1_done, switchdt_1_p3;

  not not_1 (not_1_out, CLK);
  // SwitchDT switchdt_1: pin names not known; wires that end beside it: nCLK, not_1_out, switchdt_1_p3
  Step_Counter step_counter_1 (
    .CLK(switchdt_1_p3), .nRESET(nRESET), .EN(substep_counter_1_done), .nOPDONE(nOPDONE), .COUNT(STEP));
  Substep_Counter substep_counter_1 (
    .nCLK(switchdt_1_p3), .nRESET(nRESET), .CLK(CLK), .LEN(LEN), .LAST(LASTSUBSTEP), .nDONE(nSTEPDONE),
    .DVAL(SUBSTEP), .DONE(substep_counter_1_done));
  and and_1 (and_1_out, LASTSUBSTEP, LASTSTEP);
  D_FF d_ff_1 (.D(and_1_out), .C(CLK), .nQ(nOPDONE));  // open: Q

  // Notes on the sheet:
  //   LASTSTEP: default 1
endmodule

/* Test case:
CLK ~CLK ~OPDONE ~RESET LEN8 LEN32  STEP ~LASTSUB ~SUBDONE

0   1    1       0      0    0      0    0        X

1   0    1       1      0    0      0    0        X
0   1    1       1      0    0      1    0        X

1   0    1       1      0    0      1    0        X
0   1    1       1      0    0      2    0        X

1   0    1       1      0    0      2    0        X
0   1    1       1      1    0      3    1        0

loop (i,6)
1   0    1       1      1    0      3    1        1
0   1    1       1      1    0      3    1        1
end loop

1   0    1       1      1    0      3    1        1
0   1    1       1      1    0      3    0        1

1   0    1       1      1    0      3    0        0
0   1    1       1      0    0      4    0        0

1   0    1       1      0    0      4    0        0
0   1    1       1      0    1      5    1        0

loop (i,30)
1   0    1       1      0    1      5    1        1
0   1    1       1      0    1      5    1        1
end loop

1   0    1       1      0    1      5    1        1
0   1    1       1      0    1      5    0        1

1   0    1       1      0    1      5    0        0
0   1    1       1      0    1      6    1        0

loop (i,30)
1   0    1       1      0    1      6    1        1
0   1    1       1      0    1      6    1        1
end loop

1   0    1       1      0    1      6    1        1
0   1    1       1      0    1      6    0        1

1   0    1       1      0    1      6    0        0
0   1    1       1      1    0      7    1        0
  
loop (i,6)
1   0    1       1      1    0      7    1        1
0   1    1       1      1    0      7    1        1
end loop

1   0    1       1      1    0      7    1        1
0   1    1       1      1    0      7    0        1

1   0    1       1      1    0      7    0        0
0   1    1       1      0    0      8    0        0

1   0    1       1      0    0      8    0        0
0   1    0       1      1    0      9    1        0

loop (i,6)
1   0    0       1      1    0      9    1        1
0   1    0       1      1    0      9    1        1
end loop

1   0    0       1      1    0      9    1        1
0   1    0       1      1    0      9    0        1

1   0    0       1      1    0      9    0        0
0   1    1       1      0    0      0    0        0
*/
