// Digital circuit Interrupt-Controller.dig as structural Verilog
module Interrupt_Controller (
  input  BUS_CLK,
  input  OP_LATCH,
  input  nTRAP,
  input  nRESET,
  output TRAP_OP,
  output TRAP_OP_FETCH
);

  wire not_1_out;

  not not_1 (not_1_out, OP_LATCH);
  D_FF_AS #(.Default(1)) d_ff_as_1 (
    .Set(~nRESET), .D(nTRAP), .C(not_1_out), .Clr(~1'b1), .nQ(TRAP_OP_FETCH));  // open: Q
  Imm32 u_trap_op (.CLK(BUS_CLK), .nRESET(nRESET), .LATCH(BUS_CLK), .SnP(not_1_out), .Val(32'h300073), .OUT(TRAP_OP));
endmodule
