// Digital circuit Mem.dig as structural Verilog
module Mem (
  input  CLK,
  input  nCLK,
  input  BUS_CLK,
  input  IN,
  input  ADDR_IN,
  input  ADDR_LATCH,
  input  ADDR_CLK,
  input  nOE,
  input  nWE,
  input  nS_EXT,
  input  nRESET,
  output OUT,
  output [7:0] DATA,
  output [15:0] DATA_ADDR,
  output CS_ROM,
  output CS_RAM,
  output CS_IO,
  output [31:0] DAddr,
  output [7:0] DVal
);

  wire d_ff_1_nq, d_ff_2_nq, d_ff_as_1_nq, d_ff_as_1_q, nor_1_out, SIGN;

  D_FF_AS d_ff_as_1 (.Set(~nRESET), .D(nWE), .C(CLK), .Clr(~nWE), .Q(d_ff_as_1_q), .nQ(d_ff_as_1_nq));
  D_FF #(.Default(1)) d_ff_1 (.D(ADDR_LATCH), .C(CLK), .nQ(d_ff_1_nq));  // open: Q
  _74HC595 _74hc595_1 (
    .SER(IN), .SRCLK(BUS_CLK), .nSRCLR(nRESET), .RCLK(d_ff_as_1_nq), .nOE(d_ff_as_1_q), .VCC(1'b1),
    .GND(1'b0), .QH(DATA[0]), .QG(DATA[1]), .QF(DATA[2]), .QE(DATA[3]), .QD(DATA[4]), .QC(DATA[5]),
    .QB(DATA[6]), .QA(DATA[7]));  // open: QH_2
  Mem_addr mem_addr_1 (
    .CLK(BUS_CLK), .IN(ADDR_IN), .LATCH(ADDR_LATCH), .ADDR_CLK(ADDR_CLK), .nPE(d_ff_1_nq), .nRESET(nRESET),
    .ADDR(DAddr));
  PullDown #(.Bits(8)) pulldown_1 (.out(DATA));
  Demultiplexer #(.Selector_Bits(2), .Default(1)) demultiplexer_1 (
    .sel(DAddr[31:30]), .in(1'b0), .out_0(CS_ROM), .out_2(CS_RAM), .out_3(CS_IO));  // open: out_1
  nor nor_1 (nor_1_out, nCLK, nOE);
  D_FF #(.Default(1)) d_ff_2 (.D(DATA[7]), .C(nor_1_out), .nQ(d_ff_2_nq));  // open: Q
  nor nor_2 (SIGN, nS_EXT, d_ff_2_nq);
  _74HC597 _74hc597_1 (
    .nMR(nRESET), .SHCP(BUS_CLK), .DS(SIGN), .STCP(nor_1_out), .nPL(nOE), .D7(DATA[0]), .D6(DATA[1]),
    .D5(DATA[2]), .D4(DATA[3]), .D3(DATA[4]), .D2(DATA[5]), .D1(DATA[6]), .D0(DATA[7]), .Q7(OUT), .Val(DVal));

  assign DATA_ADDR = DAddr[15:0];

  // Notes on the sheet:
  //   nOE: default 1
  //   nWE: default 1
  //   Can also set RCLK to 
  //   ~{WE} through an inverter
  //   if FF has no ~{Q} output
endmodule

/* Test case:
CLK BUS-CLK IN         ~OE ~WE ADDR-IN      ADDR-LATCH ADDR-CLK ~{ADDR-PE} ~RESET   OUT

0   0       0          1   1   0            0          0        1          0        0

loop (rep,32)

let addr = 0x80000000 | random(256);
let d0 = random(256);
let d1 = random(256);
let d2 = random(256);
let d3 = random(256);

# Output address
loop (i,32)
0   0       0          1   1   (addr>>i&1)  0          0        0          1        X
1   1       0          1   1   (addr>>i&1)  0          0        0          1        X
end loop

# Latch address
0   0       0          1   1   0            1          0        0          1        X
1   0       0          1   1   0            1          1        0          1        X

# Output data
loop (i,8)
0   0       (d0>>i&1)  1   1   0            0          0        1          1        X
1   1       (d0>>i&1)  1   1   0            0          0        1          1        X
end loop

# Latch data and write
0   0       0          1   1   0            0          0        1          1        X
0   0       0          1   0   0            0          0        1          1        X

# Output data and increase address
loop (i,8)
0   0       (d1>>i&1)  1   1   0            0          1        1          1        X
1   1       (d1>>i&1)  1   1   0            0          1        1          1        X
end loop

# Latch data and write
0   0       0          1   1   0            0          0        1          1        X
0   0       0          1   0   0            0          0        1          1        X

# Output data and increase address
loop (i,8)
0   0       (d2>>i&1)  1   1   0            0          1        1          1        X
1   1       (d2>>i&1)  1   1   0            0          1        1          1        X
end loop

# Latch data and write
0   0       0          1   1   0            0          0        1          1        X
0   0       0          1   0   0            0          0        1          1        X

# Output data and increase address
loop (i,8)
0   0       (d3>>i&1)  1   1   0            0          1        1          1        X
1   1       (d3>>i&1)  1   1   0            0          1        1          1        X
end loop

# Latch data and write
0   0       0          1   1   0            0          0        1          1        X
0   0       0          1   0   0            0          0        1          1        X

# Output address
loop (i,32)
0   0       0          1   1   (addr>>i&1)  0          0        0          1        X
1   1       0          1   1   (addr>>i&1)  0          0        0          1        X
end loop

# Latch address
0   0       0          1   1   0            1          0        0          1        X
1   0       0          1   1   0            1          1        0          1        X

# Enable output and latch
0   0       0          0   1   0            0          0        1          1        X
1   0       0          0   1   0            0          0        1          1        X

# Output data and increase address
loop (i,8)
0   0       0          1   1   0            0          1        1          1        (d0>>i&1)
1   1       0          1   1   0            0          1        1          1        X
end loop

# Enable output and latch
0   0       0          0   1   0            0          0        1          1        X
1   0       0          0   1   0            0          0        1          1        X

# Output data and increase address
loop (i,8)
0   0       0          1   1   0            0          1        1          1        (d1>>i&1)
1   1       0          1   1   0            0          1        1          1        X
end loop

# Enable output and latch
0   0       0          0   1   0            0          0        1          1        X
1   0       0          0   1   0            0          0        1          1        X

# Output data and increase address
loop (i,8)
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*/
