// Digital circuit PC.dig as structural Verilog
module PC (
  input  CLK,
  input  BUS_CLK,
  input  IN,
  input  IN_LATCH,
  input  OUT_LATCH,
  input  OUT_SnP,
  input  CNT_EN,
  input  CNT_2,
  input  nRESET,
  output OUT,
  output [31:0] PC
);

  wire _74161_1_p12, _74161_2_p12, _74161_3_p12, _74161_4_p12, _74161_5_p12, _74161_6_p12, _74161_7_p12,
       _74595_1_p1, _74595_1_p8, _74595_1_p9, _74595_1_p10, _74595_1_p11, _74595_1_p12, _74595_1_p13,
       _74595_1_p14, _74595_2_p1, _74595_2_p8, _74595_2_p9, _74595_2_p10, _74595_2_p11, _74595_2_p12,
       _74595_2_p13, _74595_2_p14, _74595_2_p15, _74595_3_p1, _74595_3_p8, _74595_3_p9, _74595_3_p10,
       _74595_3_p11, _74595_3_p12, _74595_3_p13, _74595_3_p14, _74595_3_p15, _74595_4_p8, _74595_4_p9,
       _74595_4_p10, _74595_4_p11, _74595_4_p12, _74595_4_p13, _74595_4_p14, _74595_4_p15, _74597_1_p3,
       _74597_2_p3, _74597_3_p3, d_ff_as_1_q, d_ff_as_2_nq, multiplexer_1_out, nand_1_out, nIN_LATCH,
       or_1_out, xor_1_out;

  or or_1 (or_1_out, IN_LATCH, CNT_EN);
  not not_1 (nIN_LATCH, IN_LATCH);
  D_FF_AS d_ff_as_1 (.Set(1'b0), .D(or_1_out), .C(CLK), .Clr(~nRESET), .Q(d_ff_as_1_q));  // open: nQ
  // _74595 _74595_1: pin names not known; wires that end beside it: _74595_1_p1, BUS_CLK, nRESET, IN_LATCH, 1'b0, 1'b1, 1'b0, _74595_1_p8, _74595_1_p9, _74595_1_p10, _74595_1_p11, _74595_1_p12, _74595_1_p13, _74595_1_p14
  // _74595 _74595_2: pin names not known; wires that end beside it: _74595_2_p1, BUS_CLK, nRESET, IN_LATCH, 1'b0, 1'b1, 1'b0, _74595_2_p8, _74595_2_p9, _74595_2_p10, _74595_2_p11, _74595_2_p12, _74595_2_p13, _74595_2_p14, _74595_2_p15, _74595_1_p1
  // _74595 _74595_3: pin names not known; wires that end beside it: _74595_3_p1, BUS_CLK, nRESET, IN_LATCH, 1'b0, 1'b1, 1'b0, _74595_3_p8, _74595_3_p9, _74595_3_p10, _74595_3_p11, _74595_3_p12, _74595_3_p13, _74595_3_p14, _74595_3_p15, _74595_2_p1
  // _74595 _74595_4: pin names not known; wires that end beside it: IN, BUS_CLK, nRESET, IN_LATCH, 1'b0, 1'b1, 1'b0, _74595_4_p8, _74595_4_p9, _74595_4_p10, _74595_4_p11, _74595_4_p12, _74595_4_p13, _74595_4_p14, _74595_4_p15, _74595_3_p1
  xor xor_1 (xor_1_out, PC[1], CNT_2);
  Multiplexer multiplexer_1 (.sel(CNT_EN), .in_0(_74595_1_p8), .in_1(xor_1_out), .out(multiplexer_1_out));
  D_FF_AS d_ff_as_2 (.Set(1'b0), .D(multiplexer_1_out), .C(d_ff_as_1_q), .Clr(~nRESET), .Q(PC[1]), .nQ(d_ff_as_2_nq));
  nand nand_1 (nand_1_out, CNT_2, d_ff_as_2_nq);
  // _74161 _74161_1: pin names not known; wires that end beside it: nIN_LATCH, nRESET, CLK, nand_1_out, CNT_EN, _74595_1_p9, _74595_1_p10, _74595_1_p11, _74595_1_p12, 1'b1, 1'b0, _74161_1_p12, PC[2], PC[3], PC[4], PC[5]
  // _74161 _74161_2: pin names not known; wires that end beside it: nIN_LATCH, nRESET, CLK, _74161_1_p12, CNT_EN, _74595_1_p13, _74595_1_p14, _74595_2_p8, _74595_2_p9, 1'b1, 1'b0, _74161_2_p12, PC[6], PC[7], PC[8], PC[9]
  // _74161 _74161_3: pin names not known; wires that end beside it: nIN_LATCH, nRESET, CLK, _74161_2_p12, CNT_EN, _74595_2_p10, _74595_2_p11, _74595_2_p12, _74595_2_p13, 1'b1, 1'b0, _74161_3_p12, PC[10], PC[11], PC[12], PC[13]
  // _74161 _74161_4: pin names not known; wires that end beside it: nIN_LATCH, nRESET, CLK, _74161_3_p12, CNT_EN, _74595_2_p14, _74595_2_p15, _74595_3_p8, _74595_3_p9, 1'b1, 1'b0, _74161_4_p12, PC[14], PC[15], PC[16], PC[17]
  // _74161 _74161_5: pin names not known; wires that end beside it: nIN_LATCH, nRESET, CLK, _74161_4_p12, CNT_EN, _74595_3_p10, _74595_3_p11, _74595_3_p12, _74595_3_p13, 1'b1, 1'b0, _74161_5_p12, PC[18], PC[19], PC[20], PC[21]
  // _74161 _74161_6: pin names not known; wires that end beside it: nIN_LATCH, nRESET, CLK, _74161_5_p12, CNT_EN, _74595_3_p14, _74595_3_p15, _74595_4_p8, _74595_4_p9, 1'b1, 1'b0, _74161_6_p12, PC[22], PC[23], PC[24], PC[25]
  // _74161 _74161_7: pin names not known; wires that end beside it: nIN_LATCH, nRESET, CLK, _74161_6_p12, CNT_EN, _74595_4_p10, _74595_4_p11, _74595_4_p12, _74595_4_p13, 1'b1, 1'b0, _74161_7_p12, PC[26], PC[27], PC[28], PC[29]
  // _74161 _74161_8: pin names not known; wires that end beside it: nIN_LATCH, nRESET, CLK, _74161_7_p12, CNT_EN, _74595_4_p14, _74595_4_p15, 1'b0, 1'b0, 1'b1, 1'b0, PC[30], PC[31]
  // _74597 _74597_1: pin names not known; wires that end beside it: nRESET, BUS_CLK, _74597_1_p3, OUT_LATCH, OUT_SnP, 1'b0, PC[1], PC[2], PC[3], PC[4], PC[5], PC[6], PC[7], OUT
  // _74597 _74597_2: pin names not known; wires that end beside it: nRESET, BUS_CLK, _74597_2_p3, OUT_LATCH, OUT_SnP, PC[8], PC[9], PC[10], PC[11], PC[12], PC[13], PC[14], PC[15], _74597_1_p3
  // _74597 _74597_3: pin names not known; wires that end beside it: nRESET, BUS_CLK, _74597_3_p3, OUT_LATCH, OUT_SnP, PC[16], PC[17], PC[18], PC[19], PC[20], PC[21], PC[22], PC[23], _74597_2_p3
  // _74597 _74597_4: pin names not known; wires that end beside it: nRESET, BUS_CLK, 1'b0, OUT_LATCH, OUT_SnP, PC[24], PC[25], PC[26], PC[27], PC[28], PC[29], PC[30], PC[31], _74597_3_p3

  assign PC[0] = 1'b0;
endmodule

/* Test case:
CLK BUS-CLK IN         IN-LATCH OUT-LATCH OUT-S~P CNT-EN CNT-2    ~RESET   OUT          PC

loop (rep, 32)

let PC = (random(1<<30) << 2)+2;

0   0       0          0        0         0       0      0        0       X            X

# Input PC

loop (i,32)
0   0       (PC>>i&1)  0        0         0       0      0        1       X            X
1   1       (PC>>i&1)  0        0         0       0      0        1       X            X
end loop

# Latch in

0   0       0          1        0         0       0      0        1       X            X
1   0       0          1        0         0       0      0        1       X            (PC)

# Latch out and load

0   0       0          0        1         0       0      0        1       X            X
1   0       0          0        1         0       0      0        1       X            (PC)

# Output PC

loop (i,32)
0   0       0          0        0         1       0      0        1       (PC>>i&1)    X
1   1       0          0        0         1       0      0        1       X            X
end loop

# Increase PC by 4

0   0       0          0        0         0       1      0        1       X            X
1   0       0          0        0         0       1      0        1       X            X

# Output old PC

loop (i,32)
0   0       0          0        0         1       0      0        1       (PC>>i&1)    X
1   1       0          0        0         1       0      0        1       X            X
end loop

# Latch out and load new PC

0   0       0          0        1         0       0      0        1       X            X
1   0       0          0        1         0       0      0        1       X            X

# Output PC

loop (i,32)
0   0       0          0        0         1       0      0        1       ((PC+4)>>i&1) X
1   1       0          0        0         1       0      0        1       X             X
end loop

# Increase PC by 2

0   0       0          0        0         0       1      1        1       X            X
1   0       0          0        0         0       1      1        1       X            X

# Output old PC

loop (i,32)
0   0       0          0        0         1       0      0        1       ((PC+4)>>i&1) X
1   1       0          0        0         1       0      0        1       X             X
end loop

# Latch out and load new PC

0   0       0          0        1         0       0      0        1       X             X
1   0       0          0        1         0       0      0        1       X             X

# Output PC

loop (i,32)
0   0       0          0        0         1       0      0        1       ((PC+6)>>i&1) X
1   1       0          0        0         1       0      0        1       X             X
end loop

end loop
*/
