// Digital circuit Substep-Counter.dig as structural Verilog
module Substep_Counter (
  input  nCLK,
  input  CLK,
  input  nLEN4,
  input  EN,
  input  nRESET,
  output LAST_SUBSTEP,
  output nSTEP_DONE,
  output [7:0] DVAL,
  output STEP_DONE
);

  wire _74161_1_pin9, switchdt_1_p2, switchdt_1_p3;

  // SwitchDT switchdt_1: pin names not known; wires that end beside it: nCLK, switchdt_1_p2, switchdt_1_p3
  not not_1 (switchdt_1_p2, CLK);
  _74161 _74161_1 (
    .pin1(1'b1), .pin2(switchdt_1_p3), .pin3(1'b1), .pin4(1'b0), .pin5(1'b0), .pin6(1'b0), .pin7(EN),
    .pin8(1'b0), .pin9(_74161_1_pin9), .pin10(1'b1), .pin11(DVAL[3]), .pin12(DVAL[2]), .pin13(DVAL[1]),
    .pin14(DVAL[0]), .pin16(1'b1));  // open: pin15
  and and_1 (_74161_1_pin9, nRESET, nSTEP_DONE);
  or or_1 (LAST_SUBSTEP, nLEN4, DVAL[2]);
  D_FF_AS d_ff_as_1 (.Set(~1'b1), .D(LAST_SUBSTEP), .C(CLK), .Clr(~nRESET), .Q(STEP_DONE), .nQ(nSTEP_DONE));

  assign DVAL[7:4] = 4'b0000;

  // Other names for the same wires on the sheet: Q0 = DVAL[0]; Q1 = DVAL[1]; Q2 = DVAL[2]; Q3 = DVAL[3]

  // Notes on the sheet:
  //   CLK: Hz: 2
endmodule

/* Test case:
CLK  ~CLK ~RESET EN ~LEN4  LAST-SUBSTEP ~{STEP-DONE} DVAL

0    1    0      1  1      X            X            X
0    1    1      1  1      1            X            X

1    0    1      1  1      1            0            X
0    1    1      1  1      1            0            X

1    0    1      1  1      1            0            X
0    1    1      1  1      1            0            X

1    0    1      1  1      1            0            X
0    1    1      1  1      1            0            X

1    0    1      1  1      1            0            X
0    1    1      1  0      0            0            X

1    0    1      1  0      0            1            X
0    1    1      1  0      0            1            X

1    0    1      1  0      0            1            X
0    1    1      1  0      0            1            X

1    0    1      1  0      0            1            X
0    1    1      1  0      1            1            X

1    0    1      1  0      1            0            X
0    1    1      1  0      0            0            X

1    0    1      1  0      0            1            X
0    1    1      1  0      0            1            X

1    0    1      1  0      0            1            X
0    1    1      1  0      0            1            X

1    0    1      1  0      0            1            X
0    1    1      1  0      1            1            X

1    0    1      1  0      1            0            X
0    1    1      1  1      1            0            X

1    0    1      1  1      1            0            X
0    1    1      1  1      1            0            X
*/
